# Fritzing sketch Radar (saved by Fritzing 0.9.3b)
breadboards: 2

parts:
  J1 = Basic Servo
  hc-sr1 = hc-sr04
  Part1 = Arduino Uno (Rev3) - ICSP
  R1 = Resistor [tolerance=±5% resistance=220 package=THT]
  Raspberry_Pi3 = Raspberry Pi 3 [part_number=RPI-3-V1.2]
  CONN1 = USB connector [package=THT]
  CONN2 = USB connector [package=THT]
  J2 = T Cobbler Plus
  LED1 = LED - 5mm [color="Red (633nm)" package="5 mm [THT]"]
  LED2 = LED - 5mm [color="Green (565nm)" package="5 mm [THT]"]
  LED3 = LED - 5mm [color="Green (565nm)" package="5 mm [THT]"]
  R2 = Resistor [tolerance=±5% resistance=220 package=THT]
  R3 = Resistor [tolerance=±5% resistance=220 package=THT]
  S1 = Pushbutton [package="[THT]"]
  S2 = Pushbutton [package="[THT]"]
  R7 = Resistor [tolerance=±5% resistance=10k package=THT]
  R8 = Resistor [tolerance=±5% resistance=10k package=THT]
  R10 = Resistor [tolerance=±5% resistance=220 package=THT]
  LED5 = LED - 5mm [color="Green (565nm)" package="5 mm [THT]"]

nets:
  GND: J1.gnd, hc-sr1.GND, Part1.GND, LED5.cathode
  VCC: J1.vcc, hc-sr1.VCC, Part1.5V
  N1: J1.pulse, Part1.ICSP_MISO, Part1.D12/MISO
  N2: hc-sr1.Trig, Part1.D10_PWM/SS
  N3: hc-sr1.Echo, Part1.D11_PWM/MOSI
  N4: Part1.D4, R10.Pin_1
  N5: R1.Pin_0, LED3.anode
  3V3: Raspberry_Pi3.3v3, Raspberry_Pi3.3V3, J2.3.3V
  N6: Raspberry_Pi3.GPIO2, J2.GPIO_2
  N7: Raspberry_Pi3.GPIO3, J2.GPIO_3
  N8: Raspberry_Pi3.GPIO4, J2.GPIO_4
  N9: Raspberry_Pi3.GND, J2.GND#46, J2.GND#49, J2.GND#54, J2.GND#60, J2.GND#65, J2.GND#70, J2.GND#74, J2.GND#79
  N10: Raspberry_Pi3.GPIO17, J2.GPIO_17
  N11: Raspberry_Pi3.GPIO27, J2.GPIO_27
  N12: Raspberry_Pi3.GPIO22, J2.GPIO_22
  N13: Raspberry_Pi3.GPIO10, J2.GPIO_10
  N14: Raspberry_Pi3.GPIO9, J2.GPIO_9
  N15: Raspberry_Pi3.GPIO11, J2.GPIO_11
  N16: Raspberry_Pi3.ID_SD, J2.ID_SD
  N17: Raspberry_Pi3.GPIO5, J2.GPIO_5
  N18: Raspberry_Pi3.GPIO6, J2.GPIO_6
  N19: Raspberry_Pi3.GPIO13, J2.GPIO_13
  N20: Raspberry_Pi3.GPIO19, J2.GPIO_19
  N21: Raspberry_Pi3.GPIO26, J2.GPIO_26
  N22: Raspberry_Pi3.GPIO21, J2.GPIO_21
  N23: Raspberry_Pi3.GPIO20, J2.GPIO_20
  N24: Raspberry_Pi3.GPIO16, J2.GPIO_16
  N25: Raspberry_Pi3.GPIO12, J2.GPIO_12
  N26: Raspberry_Pi3.ID_SC, J2.ID_SC
  N27: Raspberry_Pi3.GPIO7, J2.GPIO_7
  N28: Raspberry_Pi3.GPIO8, J2.GPIO_8
  N29: Raspberry_Pi3.GPIO25, J2.GPIO_25
  N30: Raspberry_Pi3.GPIO24, J2.GPIO_24
  N31: Raspberry_Pi3.GPIO23, J2.GPIO_23
  N32: Raspberry_Pi3.GPIO18, J2.GPIO_18
  N33: Raspberry_Pi3.GPIO15, J2.GPIO_15
  N34: Raspberry_Pi3.GPIO14, J2.GPIO_14
  5V: Raspberry_Pi3.5V, J2.5V
  5V_2: CONN1.5V, CONN2.5V
  N35: CONN1.d-, CONN2.d-
  N36: CONN1.d+, CONN2.d+
  GND_2: CONN1.GND, CONN1.chassis5, CONN1.chassis6, CONN2.GND, CONN2.chassis5, CONN2.chassis6
  N37: J2.GND#5, LED1.cathode, LED2.cathode, LED3.cathode
  N38: J2.GND#8, R7.Pin_0, R8.Pin_0
  N39: J2.#19, R2.Pin_1, S1.Pin_3, S1.Pin_4, R8.Pin_1
  N40: LED1.anode, R3.Pin_0
  N41: LED2.anode, R2.Pin_0
  N42: R3.Pin_1, S2.Pin_3, S2.Pin_4, R7.Pin_1
  N43: S1.Pin_1, S1.Pin_2, S2.Pin_1, S2.Pin_2
  N44: R10.Pin_0, LED5.anode

custom parts:
  T Cobbler Plus: The T-Cobbler Plus is an add on prototyping board from Adafruit specifically designed for the Raspberry Pi B+ that can break out all those tasty power, GPIO, I2C and SPI pins from the 40-pin header onto a solderless breadboard. This set will make "cobbling together" prototypes with the Pi super easy. The T-Cobbler Plus can plug into any solderless breadboard.
